// Digital circuit ALU.dig as structural Verilog
module ALU (
  input  [31:0] A,
  input  [31:0] B,
  input  [2:0] ALUControl,
  output [31:0] Result,
  output N,
  output C,
  output V,
  output Z
);

  wire add_1_c_o, not_1_out, xnor_1_out, xor_1_out;
  wire [0:0] xor_2_out;
  wire [31:0] and_3_out, multiplexer_1_out, not_2_out, or_1_out, Sum;

  xnor xnor_1 (xnor_1_out, B[31], A[31], ALUControl[0]);
  and and_1 (V, not_1_out, xor_1_out, xnor_1_out);
  xor xor_1 (xor_1_out, Sum[31], A[31]);
  not not_1 (not_1_out, ALUControl[1]);
  and and_2 (C, add_1_c_o, not_1_out);
  assign or_1_out = A | B;  // Or or_1, 32 bits wide
  xor xor_2 (xor_2_out[0], Sum[31], V);
  assign and_3_out = A & B;  // And and_3, 32 bits wide
  assign not_2_out = ~B;  // Not not_2, 32 bits wide
  Multiplexer #(.Bits(32)) multiplexer_1 (.sel(ALUControl[0]), .in_0(B), .in_1(not_2_out), .out(multiplexer_1_out));
  Add #(.Bits(32)) add_1 (.a(A), .b(multiplexer_1_out), .c_i(ALUControl[0]), .s(Sum), .c_o(add_1_c_o));
  Multiplexer #(.Selector_Bits(3), .Bits(32)) multiplexer_2 (
    .sel(ALUControl), .in_0(Sum), .in_1(Sum), .in_2(and_3_out), .in_3(or_1_out), .in_4({32{1'b0}}),
    .in_5({{31{1'b0}}, xor_2_out[0]}), .in_6({32{1'b0}}), .in_7({32{1'b0}}), .out({N, Result[30:0]}));
  Comparator #(.Bits(32)) comparator_1 (.a({N, Result[30:0]}), .b({32{1'b0}}), .eq(Z));  // open: gt, lt

  assign Result[31] = N;
endmodule
