// Digital circuit D_to_E.dig as structural Verilog
module D_to_E (
  input  [31:0] DaD,
  input  [31:0] DbD,
  input  clk,
  input  en,
  input  [31:0] ImmExtD,
  input  [31:0] PCPlus4D,
  input  [31:0] PCD,
  input  [4:0] RdD,
  input  RegWriteD,
  input  [1:0] ResultSrcD,
  input  MemWriteD,
  input  JumpD,
  input  [31:0] BranchD,
  input  [2:0] ALUControlD,
  input  ALUSrcD,
  input  [4:0] Rs1D,
  input  [4:0] Rs2D,
  input  [31:0] CLR,
  output [31:0] DaE,
  output [31:0] DbE,
  output [31:0] PCPlus4E,
  output [31:0] ImmExtE,
  output [31:0] PCE,
  output [4:0] RdE,
  output [31:0] RegWriteE,
  output [1:0] ResultSrcE,
  output MemWriteE,
  output [31:0] JumpE,
  output BranchE,
  output [2:0] ALUControlE,
  output ALUSrcE,
  output [4:0] Rs1E,
  output [4:0] Rs2E
);

  wire multiplexer_7_out, multiplexer_9_out, multiplexer_10_out, multiplexer_11_out, multiplexer_13_out;
  wire [1:0] multiplexer_8_out;
  wire [2:0] multiplexer_12_out;
  wire [4:0] multiplexer_6_out, multiplexer_14_out, multiplexer_15_out;
  wire [31:0] multiplexer_1_out, multiplexer_2_out, multiplexer_3_out, multiplexer_4_out, multiplexer_5_out;

  Multiplexer #(.Bits(32)) multiplexer_1 (.sel(CLR[0]), .in_0(DaD), .in_1({32{1'b0}}), .out(multiplexer_1_out));
  Multiplexer #(.Bits(32)) multiplexer_2 (.sel(CLR[0]), .in_0(DbD), .in_1({32{1'b0}}), .out(multiplexer_2_out));
  Multiplexer #(.Bits(32)) multiplexer_3 (.sel(CLR[0]), .in_0(ImmExtD), .in_1({32{1'b0}}), .out(multiplexer_3_out));
  Multiplexer #(.Bits(32)) multiplexer_4 (.sel(CLR[0]), .in_0(PCD), .in_1({32{1'b0}}), .out(multiplexer_4_out));
  Multiplexer #(.Bits(32)) multiplexer_5 (.sel(CLR[0]), .in_0(PCPlus4D), .in_1({32{1'b0}}), .out(multiplexer_5_out));
  Multiplexer #(.Bits(5)) multiplexer_6 (.sel(CLR[0]), .in_0(RdD), .in_1({5{1'b0}}), .out(multiplexer_6_out));
  Multiplexer multiplexer_7 (.sel(CLR[0]), .in_0(RegWriteD), .in_1(1'b0), .out(multiplexer_7_out));
  Multiplexer #(.Bits(2)) multiplexer_8 (.sel(CLR[0]), .in_0(ResultSrcD), .in_1(2'b00), .out(multiplexer_8_out));
  Multiplexer multiplexer_9 (.sel(CLR[0]), .in_0(MemWriteD), .in_1(1'b0), .out(multiplexer_9_out));
  Multiplexer multiplexer_10 (.sel(CLR[0]), .in_0(JumpD), .in_1(1'b0), .out(multiplexer_10_out));
  Multiplexer multiplexer_11 (.sel(CLR[0]), .in_0(BranchD[0]), .in_1(1'b0), .out(multiplexer_11_out));
  Multiplexer #(.Bits(3)) multiplexer_12 (.sel(CLR[0]), .in_0(ALUControlD), .in_1(3'b000), .out(multiplexer_12_out));
  Multiplexer multiplexer_13 (.sel(CLR[0]), .in_0(ALUSrcD), .in_1(1'b0), .out(multiplexer_13_out));
  Multiplexer #(.Bits(5)) multiplexer_14 (.sel(CLR[0]), .in_0(Rs1D), .in_1({5{1'b0}}), .out(multiplexer_14_out));
  Multiplexer #(.Bits(5)) multiplexer_15 (.sel(CLR[0]), .in_0(Rs2D), .in_1({5{1'b0}}), .out(multiplexer_15_out));
  Register #(.Bits(32)) register_1 (.D(multiplexer_1_out), .C(clk), .en(en), .Q(DaE));
  Register #(.Bits(32)) register_2 (.D(multiplexer_2_out), .C(clk), .en(en), .Q(DbE));
  Register #(.Bits(32)) register_3 (.D(multiplexer_3_out), .C(clk), .en(en), .Q(ImmExtE));
  Register #(.Bits(32)) register_4 (.D(multiplexer_4_out), .C(clk), .en(en), .Q(PCE));
  Register #(.Bits(32)) register_5 (.D(multiplexer_5_out), .C(clk), .en(en), .Q(PCPlus4E));
  Register #(.Bits(5)) register_6 (.D(multiplexer_6_out), .C(clk), .en(en), .Q(RdE));
  Register register_7 (.D(multiplexer_7_out), .C(clk), .en(en), .Q(RegWriteE[0]));
  Register #(.Bits(2)) register_8 (.D(multiplexer_8_out), .C(clk), .en(en), .Q(ResultSrcE));
  Register register_9 (.D(multiplexer_9_out), .C(clk), .en(en), .Q(MemWriteE));
  Register register_10 (.D(multiplexer_10_out), .C(clk), .en(en), .Q(JumpE[0]));
  Register register_11 (.D(multiplexer_11_out), .C(clk), .en(en), .Q(BranchE));
  Register #(.Bits(3)) register_12 (.D(multiplexer_12_out), .C(clk), .en(en), .Q(ALUControlE));
  Register register_13 (.D(multiplexer_13_out), .C(clk), .en(en), .Q(ALUSrcE));
  Register #(.Bits(3)) register_14 (.D(multiplexer_14_out[2:0]), .C(clk), .en(en), .Q(Rs1E[2:0]));
  Register register_15 (.D(multiplexer_15_out[0]), .C(clk), .en(en), .Q(Rs2E[0]));
  // Pins of 1 and 32 bits meet at RegWriteE
  // Pins of 1 and 32 bits meet at JumpE
  // Pins of 1 and 32 bits meet at BranchD
  // Pins of 1 and 32 bits meet at CLR
  // Pins of 5 and 32 bits meet at {32{1'b0}}
  // Pins of 1 and 32 bits meet at {32{1'b0}}
  // Pins of 2 and 32 bits meet at {32{1'b0}}
  // Pins of 1 and 32 bits meet at {32{1'b0}}
  // Pins of 1 and 32 bits meet at {32{1'b0}}
  // Pins of 1 and 32 bits meet at {32{1'b0}}
  // Pins of 3 and 32 bits meet at {32{1'b0}}
  // Pins of 1 and 32 bits meet at {32{1'b0}}
endmodule
