// Digital circuit E_to_M.dig as structural Verilog
module E_to_M (
  input  [31:0] WriteDataE,
  input  [31:0] ALUResE,
  input  clk,
  input  en,
  input  [31:0] PCPlus4E,
  input  [31:0] RdE,
  input  RegWriteE,
  input  [1:0] ResultSrcE,
  input  MemWriteE,
  output [31:0] WriteDataM,
  output [31:0] ALUResM,
  output [31:0] PCPlus4M,
  output [31:0] RdM,
  output RegWriteM,
  output [1:0] ResultSrcM,
  output MemWriteM
);

  Register #(.Bits(32)) register_1 (.D(WriteDataE), .C(clk), .en(en), .Q(WriteDataM));
  Register #(.Bits(32)) register_2 (.D(ALUResE), .C(clk), .en(en), .Q(ALUResM));
  Register #(.Bits(32)) register_3 (.D(PCPlus4E), .C(clk), .en(en), .Q(PCPlus4M));
  Register #(.Bits(32)) register_4 (.D(RdE), .C(clk), .en(en), .Q(RdM));
  Register register_5 (.D(RegWriteE), .C(clk), .en(en), .Q(RegWriteM));
  Register #(.Bits(2)) register_6 (.D(ResultSrcE), .C(clk), .en(en), .Q(ResultSrcM));
  Register register_7 (.D(MemWriteE), .C(clk), .en(en), .Q(MemWriteM));
endmodule
