// Digital circuit F_to_D.dig as structural Verilog
module F_to_D (
  input  [31:0] InstrF,
  input  [31:0] PCF,
  input  [31:0] PCPlus4F,
  input  clk,
  input  en,
  input  CLR,
  output [31:0] InstrD,
  output [31:0] PCD,
  output [31:0] PCPlus4D
);

  wire [31:0] multiplexer_1_out, multiplexer_2_out, multiplexer_3_out;

  Multiplexer #(.Bits(32)) multiplexer_1 (.sel(CLR), .in_0(InstrF), .in_1({32{1'b0}}), .out(multiplexer_1_out));
  Multiplexer #(.Bits(32)) multiplexer_2 (.sel(CLR), .in_0(PCF), .in_1({32{1'b0}}), .out(multiplexer_2_out));
  Multiplexer #(.Bits(32)) multiplexer_3 (.sel(CLR), .in_0(PCPlus4F), .in_1({32{1'b0}}), .out(multiplexer_3_out));
  Register #(.Bits(32)) register_1 (.D(multiplexer_1_out), .C(clk), .en(en), .Q(InstrD));
  Register #(.Bits(32)) register_2 (.D(multiplexer_2_out), .C(clk), .en(en), .Q(PCD));
  Register #(.Bits(32)) register_3 (.D(multiplexer_3_out), .C(clk), .en(en), .Q(PCPlus4D));
endmodule
