// Digital circuit M_to_W.dig as structural Verilog
module M_to_W (
  input  [31:0] ALUResM,
  input  [31:0] MemDataM,
  input  clk,
  input  en,
  input  [31:0] PCPlus4M,
  input  [31:0] RdM,
  input  [1:0] ResultSrcM,
  input  [1:0] RegWriteM,
  output [31:0] ALUResW,
  output [31:0] MemDataW,
  output [31:0] PCPlus4W,
  output [31:0] RdW,
  output RegWriteW,
  output [1:0] ResultSrcW
);

  Register #(.Bits(32)) register_1 (.D(MemDataM), .C(clk), .en(en), .Q(MemDataW));
  Register #(.Bits(32)) register_2 (.D(ALUResM), .C(clk), .en(en), .Q(ALUResW));
  Register #(.Bits(32)) register_3 (.D(PCPlus4M), .C(clk), .en(en), .Q(PCPlus4W));
  Register #(.Bits(32)) register_4 (.D(RdM), .C(clk), .en(en), .Q(RdW));
  Register register_5 (.D(RegWriteM[0]), .C(clk), .en(en), .Q(RegWriteW));
  Register register_6 (.D(ResultSrcM[0]), .C(clk), .en(en), .Q(ResultSrcW[0]));
  // Pins of 1 and 2 bits meet at RegWriteM
  // Pins of 1 and 2 bits meet at ResultSrcM
  // Pins of 1 and 2 bits meet at ResultSrcW
endmodule
