// Digital circuit decoder.dig as structural Verilog
module decoder (
  input  [6:0] op,
  input  Zero,
  input  [2:0] funct3,
  input  [6:0] funct7,
  output RegWrite,
  output [1:0] ImmSrc,
  output ALUSrc,
  output MemWrite,
  output [1:0] ResultSrc,
  output Branch,
  output [1:0] ALUOp,
  output PCSrc,
  output [2:0] ALUControl,
  output Jump
);

  wire and_1_out, and_2_out;
  wire [2:0] multiplexer_1_out, multiplexer_2_out;

  and and_1 (and_1_out, op[5], funct7[5]);
  LookUpTable #(.Bits(11)) Main_Decoder (
    .in0(op[2]), .in1(op[3]), .in2(op[4]), .in3(op[5]), .in4(op[6]),
    .out({RegWrite, ImmSrc, ALUSrc, MemWrite, ResultSrc, Branch, ALUOp, Jump}));
  Multiplexer #(.Bits(3)) multiplexer_1 (.sel(and_1_out), .in_0(3'b000), .in_1(3'b001), .out(multiplexer_1_out));
  Multiplexer #(.Selector_Bits(3), .Bits(3)) multiplexer_2 (
    .sel(funct3), .in_0(multiplexer_1_out), .in_1(3'b000), .in_2(3'b101), .in_3(3'b000), .in_4(3'b000),
    .in_5(3'b000), .in_6(3'b011), .in_7(3'b010), .out(multiplexer_2_out));
  and and_2 (and_2_out, Zero, Branch);
  Multiplexer #(.Selector_Bits(2), .Bits(3)) multiplexer_3 (
    .sel(ALUOp), .in_0(3'b000), .in_1(3'b001), .in_2(multiplexer_2_out), .in_3(3'b000), .out(ALUControl));
  or or_1 (PCSrc, Jump, and_2_out);
  // Pins of 1 and 2 bits meet at ResultSrc

  // Notes on the sheet:
  //   contents of Main_Decoder (hex, n*v repeats v):
  //   490,0,0,0,484,0,0,0,1c0,0,0,0,404,11*0,20a,0,0,721
endmodule
