// Digital circuit piplined_riscv_cpu.dig as structural Verilog
module piplined_riscv_cpu (
);

  wire ALUControl, ALUControlD, ALUSrc, ALUSrcD, ALUSrcE, and_1_out, BranchD, BranchE, clk, d_to_e_1_p18,
       e_to_m_1_p10, JumpD, JumpE, MemWrite, MemWriteD, MemWriteE, MemWriteM, PCSrcE, RdE, RdM, RegWrite,
       RegWriteD, RegWriteE, RegWriteM, RegWriteW, ResultSrc, ResultSrcD, ResultSrcE, ResultSrcM, Zero, ZeroE;
  wire [1:0] ImmSrc, ResultSrcW;
  wire [2:0] ALUControlE, funct3;
  wire [4:0] RdD, RdW, Rs1D, Rs2D;
  wire [6:0] funct7, op;
  wire [23:0] PC_q;
  wire [31:0] add_1_s, add_2_s, ALU_result, d_to_e_1_p16, d_to_e_1_p17, d_to_e_1_p19, d_to_e_1_p20,
       Data_Memory_d, e_to_m_1_p8, e_to_m_1_p9, Extend_out, f_to_d_1_pcd, f_to_d_1_pcplus4d,
       Instruction_Memory_d, m_to_w_1_p7, m_to_w_1_p8, m_to_w_1_p9, multiplexer_1_out, multiplexer_2_out,
       multiplexer_3_out, multiplexer_4_out, multiplexer_5_out, Register_File_da, Register_File_db;
  wire [31:24] PC_q_2;

  Add #(.Bits(32)) add_1 (.a({PC_q_2, PC_q}), .b(32'h1), .c_i(1'b0), .s(add_1_s));  // open: c_o
  Multiplexer #(.Bits(32)) multiplexer_1 (.sel(PCSrcE), .in_0(add_1_s), .in_1(add_2_s), .out(multiplexer_1_out));
  Register #(.Bits(32), .isProgramCounter("true")) PC (.D(multiplexer_1_out), .C(clk), .en(1'b1), .Q({PC_q_2, PC_q}));
  EEPROMDualPort #(.AddrBits(24), .isProgramMemory("true"), .Bits(32)) Instruction_Memory (
    .A(PC_q), .Din({32{1'b0}}), .str(1'b0), .C(clk), .ld(1'b1), .D(Instruction_Memory_d));
  F_to_D f_to_d_1 (
    .InstrF(Instruction_Memory_d), .PCF({PC_q_2, PC_q}), .PCPlus4F(add_1_s), .clk(clk),
    .InstrD({funct7, Rs2D, Rs1D, funct3, RdD, op}), .PCD(f_to_d_1_pcd), .PCPlus4D(f_to_d_1_pcplus4d));  // open: CLR, en
  // decoder decoder_1: pin names not known; wires that end beside it: op, Zero, funct3, funct7, RegWrite, ImmSrc, ALUSrc, MemWrite, ResultSrc, BranchD, ALUControl, JumpD
  sign_extend_unit Extend (.inst_31_7({funct7, Rs2D, Rs1D, funct3, RdD}), .ImmSrc(ImmSrc), .out(Extend_out));
  RegisterFile #(.AddrBits(5), .Bits(32)) Register_File (
    .Din(multiplexer_5_out), .we(RegWriteW), .Rw(RdW), .C(clk), .Ra(Rs1D), .Rb(Rs2D), .Da(Register_File_da),
    .Db(Register_File_db));
  // D_to_E d_to_e_1: pin names not known; wires that end beside it: Register_File_da, Register_File_db, Extend_out, f_to_d_1_pcplus4d, f_to_d_1_pcd, RdD, RegWriteD, ResultSrcD, MemWriteD, JumpD, BranchD, ALUControlD, ALUSrcD, Rs1D, Rs2D, d_to_e_1_p16, d_to_e_1_p17, d_to_e_1_p18, d_to_e_1_p19, d_to_e_1_p20, RdE, RegWriteE, ResultSrcE, MemWriteE, JumpE, BranchE, ALUControlE, ALUSrcE
  Button button_1 (.out(clk));
  Multiplexer #(.Selector_Bits(2), .Bits(32)) multiplexer_2 (
    .in_0(d_to_e_1_p17), .in_1(m_to_w_1_p7), .in_2(e_to_m_1_p9), .in_3({32{1'b0}}), .out(multiplexer_2_out));  // open: sel
  or or_1 (PCSrcE, and_1_out, JumpE);
  Multiplexer #(.Selector_Bits(2), .Bits(32)) multiplexer_3 (
    .in_0(d_to_e_1_p16), .in_1(m_to_w_1_p7), .in_2(e_to_m_1_p9), .in_3({32{1'b0}}), .out(multiplexer_3_out));  // open: sel
  and and_1 (and_1_out, ZeroE, BranchE);
  Multiplexer #(.Bits(32)) multiplexer_4 (
    .sel(ALUSrcE), .in_0(multiplexer_2_out), .in_1(d_to_e_1_p19), .out(multiplexer_4_out));
  Add #(.Bits(32)) add_2 (.a(d_to_e_1_p19), .b(d_to_e_1_p20), .c_i(1'b0), .s(add_2_s));  // open: c_o
  ALU ALU (
    .A(multiplexer_3_out), .B(multiplexer_4_out), .ALUControl(ALUControlE), .Result(ALU_result), .Z(ZeroE));  // open: N, C, V
  // E_to_M e_to_m_1: pin names not known; wires that end beside it: d_to_e_1_p17, ALU_result, d_to_e_1_p18, RdE, RegWriteE, ResultSrcE, MemWriteE, e_to_m_1_p8, e_to_m_1_p9, e_to_m_1_p10, RdM, RegWriteM, ResultSrcM, MemWriteM
  EEPROMDualPort #(.AddrBits(24), .Bits(32)) Data_Memory (
    .A(e_to_m_1_p9[23:0]), .Din(e_to_m_1_p8), .str(MemWriteM), .C(clk), .ld(1'b1), .D(Data_Memory_d));
  // M_to_W m_to_w_1: pin names not known; wires that end beside it: e_to_m_1_p9, Data_Memory_d, e_to_m_1_p10, RdM, ResultSrcM, RegWriteM, m_to_w_1_p7, m_to_w_1_p8, m_to_w_1_p9, RdW, RegWriteW, ResultSrcW
  Multiplexer #(.Selector_Bits(2), .Bits(32)) multiplexer_5 (
    .sel(ResultSrcW), .in_0(m_to_w_1_p7), .in_1(m_to_w_1_p8), .in_2(m_to_w_1_p9), .in_3({32{1'b0}}),
    .out(multiplexer_5_out));

  // Notes on the sheet:
  //   contents of Instruction_Memory (hex, n*v repeats v):
  //   52283,5a303,6283b3,3ae33,e0463,c0006f,762023,c0006f,762023,40006f
  //   @abdalrahimnaser
endmodule
