// Digital circuit sign_extend_unit.dig as structural Verilog
module sign_extend_unit (
  input  [24:0] inst_31_7,
  input  [1:0] ImmSrc,
  output [31:0] out
);

  wire [31:0] bitextender_1_out, bitextender_2_out, bitextender_3_out;

  BitExtender #(.inputBits(12), .outputBits(32)) bitextender_1 (.in(inst_31_7[24:13]), .out(bitextender_1_out));
  BitExtender #(.inputBits(12), .outputBits(32)) bitextender_2 (
    .in({inst_31_7[24:18], inst_31_7[4:0]}), .out(bitextender_2_out));
  BitExtender #(.inputBits(13), .outputBits(32)) bitextender_3 (
    .in({inst_31_7[24], inst_31_7[0], inst_31_7[23:18], inst_31_7[4:1], 1'b0}), .out(bitextender_3_out));
  Multiplexer #(.Selector_Bits(2), .Bits(32)) multiplexer_1 (
    .sel(ImmSrc), .in_0(bitextender_1_out), .in_1(bitextender_2_out), .in_2(bitextender_3_out),
    .in_3({32{1'b0}}), .out(out));
endmodule
